# Fritzing sketch metronome2-piezo (saved by Fritzing 0.9.2b)
breadboards: 1

parts:
  Part1 = Arduino Uno (Rev3)
  SP1 = SPEAKER [package=pcb_mount_speaker]
  LCD1 = LCD screen
  LED1 = LEDs [package=led10mm]
  U1 = POT [package=trim_pot]
  R2 = Resistor [tolerance=±5% resistance=330 package="0805 [SMD]"]
  R3 = Resistor [tolerance=±5% resistance=330 package="0805 [SMD]"]
  R4 = Resistor [tolerance=±5% resistance=1M package=THT]
  J1 = Piezo Speaker

nets (from the breadboard view):
  N1: Part1.A0, R4.Pin_1, J1.pin2
  N2: Part1.D8, SP1.-
  N3: Part1.D11_PWM/MOSI, LCD1.E
  N4: Part1.D12/MISO, LCD1.RS
  N5: Part1.D13/SCK, LED1.C
  GND: Part1.GND, SP1.+, LCD1.VSS, LCD1.R/W, LCD1.LED-, U1.S, R3.Pin_0, R4.Pin_0, J1.pin1
  N6: Part1.D2, LCD1.DB7
  N7: Part1.D3_PWM, LCD1.DB6
  N8: Part1.D4, LCD1.DB5
  N9: Part1.D5_PWM, LCD1.DB4
  5V: Part1.5V, LCD1.VDD, U1.A, R2.Pin_0
  N10: LCD1.V0, U1.E
  N11: LCD1.LED+, R2.Pin_1
